# Fritzing sketch Circuit Diagram (saved by Fritzing 0.9.3b)

parts:
  A1 = ky-033 [package=THT]
  U1 = L9110 H-bridge module [part_number="L9110 H-bridge"]
  J1 = STM32 Nucleo boards
  A2 = ky-033 [package=THT]
  BT1 = Bluetooth HC-06u [package=THT]
  M3 = DC Mini Metal Gear Motor
  M4 = DC Mini Metal Gear Motor
  hc-sr1 = hc-sr04

nets:
  N1: A1.pin1, J1.PB0
  GND: A1.pin3, U1.MOTOR_A-B, U1.MOTOR_B-A, J1.GND, A2.pin3, BT1.GND, M3.IN2, M4.IN1
  5V: A1.pin4, U1.MOTOR_A-A, U1.MOTOR_B-B, J1.5V, A2.pin4, BT1.VCC, M3.IN1, M4.IN2
  N2: U1.B-IA, J1.A1
  N3: U1.B-IB, J1.PC3
  N4: U1.A-IA, J1.A0
  N5: U1.A-IB, J1.PC2
  N6: J1.D8, BT1.RXD
  N7: J1.D10_PWM/SS, hc-sr1.Echo
  N8: J1.D12/MISO, hc-sr1.Trig
  N9: J1.D2, BT1.TXD
  N10: J1.PB1, A2.pin1

custom parts:
  ky-033: KY-033 Line successor module with TCRT5000 and analog output.
  Bluetooth HC-06u: Bluetooth HC-06 - face up, pins down 16.5mm x 37.5mm PCB
